# Fritzing sketch Boxes (saved by Fritzing 0.9.3b)
breadboards: 1

parts:
  Part1 = Arduino Due (Rev2b)
  LED-кнопка = LEDs [package=led10mm]
  IC1 = ULN2803A [package=THT]
  НЛО = Header 2 [package=molex-1x2_lock]
  Кнопка_(Ниж_Бок_____Низ_Верх_Бок) = SWITCH_SPDT [package=kps-1290]

nets:
  N1: Part1.VIN, LED-кнопка.A, IC1.COM_-_Common, НЛО.1
  N2: Part1.D30, Кнопка_(Ниж_Бок_____Низ_Верх_Бок).S
  N3: Part1.D31, IC1.In_1
  N4: Part1.GND, IC1.0V
  N5: LED-кнопка.C, IC1.Out_1
  N6: НЛО.2, Кнопка_(Ниж_Бок_____Низ_Верх_Бок).O

notes:
  +12V
  GND
